# Fritzing sketch rangkaianalat (saved by Fritzing 1.0.5)

parts:
  DHT1 = Humidity and Temperature Sensor DHT11
  U1 = ESP8266 NodeMCU LoLin module
  LED1 = LED - 5mm [color="Green (560nm)" current=0.030A package="5 mm [THT]"]

nets:
  VCC: DHT1.Vcc, U1.3V3
  N1: DHT1.Data-signal, U1.D4
  N2: DHT1.GND_1, U1.GND, LED1.anode
  N3: U1.D5, LED1.cathode

custom parts:
  Humidity and Temperature Sensor DHT11: Digital relative humidity & temperature sensor DHT11
  ESP8266 NodeMCU LoLin module: ESP8266 based NodeMCU
